# Fritzing sketch PiDAR_2.0.1 (saved by Fritzing 1.0.2b)
breadboards: 1

parts:
  Mod1 = Raspberry Pi 4B
  A4988 = Pololu A4988 [package=SO16]
  Power_Button = Momentary Switch [package=ksa_sealed_tac_switch]
  Scan_Button = Momentary Switch [package=ksa_sealed_tac_switch]
  Stepper = Stepper Motor - Bipolar
  M1 = LDRobot LD19 Lidar [package=THT]
  U1 = Intenso XS10000 [package=XS10000]
  R1 = Resistor [tolerance=±5% power=0.25W resistance=220 package=THT]
  R2 = Resistor [tolerance=±5% power=0.25W resistance=220 package=THT]
  DS2Y-5-DC5V2 = DS2Y-5-DC5V [part_number=DS2Y-5-DC5V]
  Battery_Switch1 = Toggle Switch [package=THT]
  C1 = Electrolytic Capacitor [capacitance=2.2mF voltage=35V package="0605 [SMD, electrolytic]"]
  Boost_Convertor1 = Boost Convertor [part_number=XL6009E1 package=THT]

nets:
  N1: Mod1.5V, DS2Y-5-DC5V2.13_COM, C1.+, Boost_Convertor1.Positive_Input
  N2: Mod1.GPIO2, Mod1.GPIO3, Power_Button.1
  N3: Mod1.GND, A4988.GND#8, M1.pin3, R1.Pin_1, R2.Pin_1, DS2Y-5-DC5V2.1_+, C1.-, Boost_Convertor1.Negative_Input
  N4: Mod1.GPIO15, M1.pin1
  N5: Mod1.GPIO17, Scan_Button.1
  N6: Mod1.GPIO18, M1.pin2
  N7: Mod1.GPIO23, Mod1.GPIO24, DS2Y-5-DC5V2.16_-
  N8: Mod1.ID_SD, Mod1.GPIO5, A4988.MS1
  N9: Mod1.GPIO6, A4988.MS2
  N10: Mod1.GPIO13, A4988.MS3
  N11: Mod1.GPIO19, A4988.STEP
  N12: Mod1.GPIO26, A4988.DIR
  N13: A4988.RESET, A4988.SLEEP
  N14: A4988.VDD, M1.pin4, DS2Y-5-DC5V2.9_N.O.
  N15: A4988.1B, Stepper.B-
  N16: A4988.1A, Stepper.B+
  N17: A4988.2A, Stepper.A+
  N18: A4988.2B, Stepper.A-
  N19: A4988.GND#14, Boost_Convertor1.Negative_Output
  N20: A4988.VMOT, DS2Y-5-DC5V2.8_N.O.
  N21: Power_Button.3, R2.Pin_0
  N22: Scan_Button.3, R1.Pin_0
  N23: U1.+, Battery_Switch1.COM
  N24: DS2Y-5-DC5V2.4_COM, Boost_Convertor1.Positive_Output

custom parts:
  Stepper Motor - Bipolar: Simple, but very powerful bi polar stepper motor. 4 wire
  Intenso XS10000: 10000mAh Powerbank 91 x 63 x 22 mm 182 g
  Boost Convertor: DC to DC boost convertor
